# Fritzing sketch F1 board (saved by Fritzing 1.0.0rc)
breadboards: 2

parts:
  A1 = Particle - Photon2  # not connected
  Part1 = 16 NeoPixel Ring [part_number=1463]
  U1 = ENCODER_RGB [package=encoder_led_2]
  OLED_I2C1 = OLED 128x64 I2C Monochrome Display
  OLED_I2C2 = OLED 128x64 I2C Monochrome Display
  S1 = Pushbutton [package="[THT]"]
  S2 = Pushbutton [package="[THT]"]
  R1 = Resistor [tolerance=±5% power=0.25W resistance=10k package=THT]
  R2 = Resistor [tolerance=±5% power=0.25W resistance=10k package=THT]
  Neopixel1 = Adafruit RBG Smart Neopixel [package="DIP (Dual Inline) [THT]"]
  Neopixel2 = Adafruit RBG Smart Neopixel [package="DIP (Dual Inline) [THT]"]
  Neopixel3 = Adafruit RBG Smart Neopixel [package="DIP (Dual Inline) [THT]"]
  Neopixel4 = Adafruit RBG Smart Neopixel [package="DIP (Dual Inline) [THT]"]
  Neopixel5 = Adafruit RBG Smart Neopixel [package="DIP (Dual Inline) [THT]"]
  Neopixel6 = Adafruit RBG Smart Neopixel [package="DIP (Dual Inline) [THT]"]
  Neopixel7 = Adafruit RBG Smart Neopixel [package="DIP (Dual Inline) [THT]"]
  Neopixel8 = Adafruit RBG Smart Neopixel [package="DIP (Dual Inline) [THT]"]

nets:
  GND: Part1.GND, U1.C, OLED_I2C1.GND, OLED_I2C2.GND, R1.Pin_1, R2.Pin_1, Neopixel1.+, Neopixel2.+, Neopixel3.+, Neopixel4.+, Neopixel5.+, Neopixel6.+, Neopixel7.+, Neopixel8.+
  N1: OLED_I2C1.SDA, OLED_I2C2.SDA
  N2: OLED_I2C1.SCK, OLED_I2C2.SCK
  VDD: OLED_I2C1.VDD, OLED_I2C2.VDD, S1.Pin_3, S1.Pin_4, S2.Pin_3, S2.Pin_4
  N3: S1.Pin_1, S1.Pin_2, R1.Pin_0
  N4: S2.Pin_1, S2.Pin_2, R2.Pin_0
  N5: Neopixel1.G, Neopixel2.G, Neopixel3.G, Neopixel4.G, Neopixel5.G, Neopixel6.G, Neopixel7.G, Neopixel8.G
  N6: Neopixel1.O, Neopixel2.In
  N7: Neopixel2.O, Neopixel3.In
  N8: Neopixel3.O, Neopixel4.In
  N9: Neopixel4.O, Neopixel5.In
  N10: Neopixel5.O, Neopixel6.In
  N11: Neopixel6.O, Neopixel8.In
  N12: Neopixel7.In, Neopixel8.O

custom parts:
  Particle - Photon2: The Photon 2 is a microcontroller and Wi-Fi networking developed by particle. Features: 802.11a/b/g/n Wi-Fi, 2.4 GHz and 5 GHz Integrated PCB antenna Integrated U.FL connector for external antenna Integrated RF switch BLE 5 using same antenna as Wi-Fi Realtek RTL8721DM MCU ARM Cortex M33 CPU, 200 MHz 2048 KB (2 MB) user application maximum size 3072 KB (3 MB) of RAM available to user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
  16 NeoPixel Ring: 16 ultra bright smart LED NeoPixels are arranged in a circle with 1.75" (44.5mm) outer diameter. The rings are 'chainable' - connect the output pin of one to the input pin of another. Use only one microcontroller pin to control as many as you can chain together! Each LED is addressable as the driver chip is inside the LED. Each one has ~18mA constant current drive so the color will be very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
  ENCODER_RGB: SparkFun RGB rotary Encoder
  Pushbutton: A generic pushbutton.
